# Fritzing sketch beerPong (saved by Fritzing 0.9.3b)
breadboards: 1

parts:
  Composant1 = Arduino Mega 2560 (Rev3)
  Composant7 = 24 NeoPixel Ring [part_number=1586]  # not connected
  J8 = Generic male header - 4 pins [form="♂ (male)" package=THT]
  Composant8 = 24 NeoPixel Ring [part_number=1586]  # not connected
  J9 = Generic male header - 4 pins [form="♂ (male)" package=THT]
  Composant9 = 24 NeoPixel Ring [part_number=1586]  # not connected
  J10 = Generic male header - 4 pins [form="♂ (male)" package=THT]
  Composant10 = 24 NeoPixel Ring [part_number=1586]  # not connected
  J11 = Generic male header - 4 pins [form="♂ (male)" package=THT]
  Composant11 = 24 NeoPixel Ring [part_number=1586]  # not connected
  J12 = Generic male header - 4 pins [form="♂ (male)" package=THT]
  Composant12 = 24 NeoPixel Ring [part_number=1586]  # not connected
  J13 = Generic male header - 4 pins [form="♂ (male)" package=THT]
  Composant13 = 24 NeoPixel Ring [part_number=1586]  # not connected
  J14 = Generic male header - 4 pins [form="♂ (male)" package=THT]
  Composant14 = 24 NeoPixel Ring [part_number=1586]  # not connected
  J15 = Generic male header - 4 pins [form="♂ (male)" package=THT]
  Composant15 = 24 NeoPixel Ring [part_number=1586]  # not connected
  J16 = Generic male header - 4 pins [form="♂ (male)" package=THT]
  Composant16 = 24 NeoPixel Ring [part_number=1586]  # not connected
  J17 = Generic male header - 4 pins [form="♂ (male)" package=THT]
  J19 = Generic male header - 2 pins [form="♂ (male)" package=THT]
  J20 = Generic male header - 2 pins [form="♂ (male)" package=THT]
  J21 = Generic male header - 2 pins [form="♂ (male)" package=THT]
  J22 = Generic male header - 2 pins [form="♂ (male)" package=THT]
  J23 = Generic male header - 2 pins [form="♂ (male)" package=THT]
  J24 = Generic male header - 2 pins [form="♂ (male)" package=THT]
  J25 = Generic male header - 2 pins [form="♂ (male)" package=THT]
  J26 = Generic male header - 2 pins [form="♂ (male)" package=THT]
  J27 = Generic male header - 2 pins [form="♂ (male)" package=THT]
  PIR1 = PIR sensor
  J28 = Generic male header - 3 pins [form="♀ (female)" package=THT]
  PIR2 = PIR sensor
  J29 = Generic male header - 3 pins [form="♀ (female)" package=THT]
  PIR3 = PIR sensor
  J30 = Generic male header - 3 pins [form="♀ (female)" package=THT]
  PIR4 = PIR sensor
  J31 = Generic male header - 3 pins [form="♀ (female)" package=THT]
  PIR5 = PIR sensor
  J32 = Generic male header - 3 pins [form="♀ (female)" package=THT]
  PIR6 = PIR sensor
  J33 = Generic male header - 3 pins [form="♀ (female)" package=THT]
  PIR7 = PIR sensor
  J34 = Generic male header - 3 pins [form="♀ (female)" package=THT]
  PIR8 = PIR sensor
  J35 = Generic male header - 3 pins [form="♀ (female)" package=THT]
  PIR9 = PIR sensor
  J36 = Generic male header - 3 pins [form="♀ (female)" package=THT]
  PIR10 = PIR sensor
  BUTTON1 = Waterproof Pushbutton (green)
  VCC1 = Battery
  C2 = Electrolytic Capacitor [capacitance=0.1µF package="0807 [SMD, electrolytic]"]
  U2 = Voltage Regulator - 5V [package="DPak [SMD]"]
  C3 = Electrolytic Capacitor [package="0807 [SMD, electrolytic]"]

nets:
  GND: Composant1.GND, J19.GND, J28.GND, BUTTON1.no_name_yet#5, VCC1.-, C2.+, U2.GND, C3.+
  N1: Composant1.D11_PWM, J17.DI
  N2: Composant1.D10_PWM, J16.DI
  N3: Composant1.D9_PWM, J15.DI
  N4: Composant1.D8_PWM, J14.DI
  N5: Composant1.D2_PWM, J11.DI
  N6: Composant1.D3_PWM, J10.DI
  N7: Composant1.D4_PWM, J9.DI
  N8: Composant1.D5_PWM, J8.DI
  N9: Composant1.D6_PWM, J12.DI
  N10: Composant1.D7_PWM, J13.DI
  N11: Composant1.D22, PIR1.SIG
  N12: Composant1.D24, PIR2.SIG
  N13: Composant1.D26, PIR3.SIG
  N14: Composant1.D28, PIR4.SIG
  N15: Composant1.D30, PIR5.SIG
  N16: Composant1.D32, PIR6.SIG
  N17: Composant1.D34, PIR7.SIG
  N18: Composant1.D36, PIR8.SIG
  N19: Composant1.D38, PIR9.SIG
  N20: Composant1.D40, PIR10.SIG
  5V: J8.5V, J25.5V
  GND_2: J8.GND, J25.GND
  5V_2: J9.5V, J22.5V
  GND_3: J9.GND, J22.GND
  5V_3: J10.5V, J21.5V
  GND_4: J10.GND, J21.GND
  5V_4: J11.5V, J20.5V
  GND_5: J11.GND, J20.GND
  5V_5: J12.5V, J26.5V
  GND_6: J12.GND, J26.GND
  5V_6: J13.5V, J23.5V
  GND_7: J13.GND, J23.GND
  5V_7: J14.5V, J24.5V
  GND_8: J14.GND, J24.GND
  5V_8: J15.5V, J27.5V
  GND_9: J15.GND, J27.GND
  5V_9: J16.5V, J17.5V
  GND_10: J16.GND, J17.GND
  5V_10: J19.5V, J28.VCC, C2.-, U2.output_voltage
  VDD: PIR1.VDD, J29.VCC
  GND_11: PIR1.GND, J29.GND
  VDD_2: PIR2.VDD, J30.VCC
  GND_12: PIR2.GND, J30.GND
  VDD_3: PIR3.VDD, J31.VCC
  GND_13: PIR3.GND, J31.GND
  VDD_4: PIR4.VDD, PIR7.VDD
  GND_14: PIR4.GND, J34.GND
  VDD_5: PIR5.VDD, J33.VCC
  GND_15: PIR5.GND, J35.GND
  VCC: J32.VCC, J35.VCC
  GND_16: J32.GND, PIR6.GND
  VDD_6: PIR6.VDD, J34.VCC
  GND_17: J33.GND, PIR7.GND
  VDD_7: PIR8.VDD, J36.VCC
  GND_18: PIR8.GND, J36.GND
  VDD_8: PIR9.VDD, PIR10.VDD
  GND_19: PIR9.GND, PIR10.GND
  N21: BUTTON1.no_name_yet#1, VCC1.+
  N22: BUTTON1.no_name_yet#4, U2.input_voltage, C3.c-3.3µF

custom parts:
  24 NeoPixel Ring: 24 ultra bright smart LED NeoPixels are arranged in a circle with 2.6" (66mm) outer diameter. The rings are 'chainable' - connect the output pin of one to the input pin of another. Use only one microcontroller pin to control as many as you can chain together! Each LED is addressable as the driver chip is inside the LED. Each one has ~18mA constant current drive so the color will be very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
  Generic male header - 4 pins: Generic male header
  Generic male header - 2 pins: Generic male header
  Generic male header - 3 pins: Generic male header
  Waterproof Pushbutton (green): Waterproof Illuminated Pushbutton (green)
  Electrolytic Capacitor: A smd electrolytic capacitor.
